// Logisim project trabalho_todo.circ as structural Verilog: 2 circuits, main circuit BD
module BD (
  input  [2:0] ENDERECO_S,
  input  [2:0] ENDERECO_RD,
  input  RD,
  input  [31:0] ENTRADA,
  input  CLK,
  output [31:0] S
);

  wire demultiplexer_1_out0, demultiplexer_1_out1, demultiplexer_1_out2, demultiplexer_1_out3,
       demultiplexer_1_out4, demultiplexer_1_out5, demultiplexer_1_out6, demultiplexer_1_out7;
  wire [31:0] X0_q, X1_q, X2_q, X3_q, X4_q, X5_q, X6_q, X7_q;

  Demultiplexer #(.select(3)) demultiplexer_1 (
    .out0(demultiplexer_1_out0), .out1(demultiplexer_1_out1), .out2(demultiplexer_1_out2),
    .out3(demultiplexer_1_out3), .out4(demultiplexer_1_out4), .out5(demultiplexer_1_out5),
    .out6(demultiplexer_1_out6), .out7(demultiplexer_1_out7), .in(RD), .sel(ENDERECO_RD));
  Register #(.width(32)) X0 (.D(ENTRADA), .en(demultiplexer_1_out7), .clk(CLK), .Q(X0_q));  // open: clr
  Register #(.width(32)) X1 (.D(ENTRADA), .en(demultiplexer_1_out6), .clk(CLK), .Q(X1_q));  // open: clr
  Register #(.width(32)) X2 (.D(ENTRADA), .en(demultiplexer_1_out5), .clk(CLK), .Q(X2_q));  // open: clr
  Register #(.width(32)) X3 (.D(ENTRADA), .en(demultiplexer_1_out4), .clk(CLK), .Q(X3_q));  // open: clr
  Register #(.width(32)) X4 (.D(ENTRADA), .en(demultiplexer_1_out3), .clk(CLK), .Q(X4_q));  // open: clr
  Register #(.width(32)) X5 (.D(ENTRADA), .en(demultiplexer_1_out2), .clk(CLK), .Q(X5_q));  // open: clr
  Register #(.width(32)) X6 (.D(ENTRADA), .en(demultiplexer_1_out1), .clk(CLK), .Q(X6_q));  // open: clr
  Register #(.width(32)) X7 (.D(ENTRADA), .en(demultiplexer_1_out0), .clk(CLK), .Q(X7_q));  // open: clr
  Multiplexer #(.select(3), .width(32)) multiplexer_1 (
    .in0(X0_q), .in1(X1_q), .in2(X2_q), .in3(X3_q), .in4(X4_q), .in5(X5_q), .in6(X6_q), .in7(X7_q), .out(S),
    .sel(ENDERECO_S));
endmodule

module main (
);

  BD bd_1 ();  // open: ENDERECO_S, ENDERECO_RD, RD, ENTRADA, CLK, S
endmodule
